# Fritzing sketch Circuit Connections (saved by Fritzing 0.8.7b)

parts:
  Part1 = Arduino Uno (Rev3)
  U1 = ESP8266 WiFi Module [part_number=ESP8266]
  KY-1 = Keyes Relay [package=THT]
  Part4 = Lilypad Battery Connect
  LED1 = LEDs [package=led10mm]

nets:
  GND: Part1.GND, U1.GND, KY-1.ground
  N1: Part1.D2, U1.TXD
  N2: Part1.D3_PWM, U1.RXD
  N3: Part1.D7, KY-1.signal
  N4: Part1.5V, KY-1.power
  N5: U1.VCC, U1.CH_PD
  N6: KY-1.C, Part4.+
  N7: KY-1.NO, LED1.A
  N8: Part4.-, LED1.C

notes:
  AC
  Power Supply

custom parts:
  ESP8266 WiFi Module: Generic WiFi Module based on the ESP8266 with onboard PCB antenna and UART communications
  Keyes Relay: The Keyes 5V relay module is suitable for SCM development, home appliance control. It uses a 5V~12V TIL control signal which can control DC / AC signal.
  LEDs: LEDs Standard schematic elements and footprints for 5mm, 3mm, 1206, and 0603 sized LEDs. 5mm - Spark Fun Electronics SKU : COM-00529 (and others)
